# Fritzing sketch riego (saved by Fritzing 0.9.3b)
circuit board: 10cm x 10cm

parts:
  U1 = ESP32-38PinWide [part_number=ESP32-38PinWide]
  Q5 = Basic FET N-Channel [part_number=IRF520N package="TO220 [THT]"]
  R10 = Resistor [tolerance=±5% resistance=1k package=THT]
  LED5 = LED - 5mm [color="Red (633nm)" package="5 mm [THT]"]
  R9 = Resistor [tolerance=±5% resistance=1k package=THT]
  Q6 = Basic FET N-Channel [part_number=IRF520N package="TO220 [THT]"]
  R11 = Resistor [tolerance=±5% resistance=1k package=THT]
  R12 = Resistor [tolerance=±5% resistance=1k package=THT]
  LED6 = LED - 5mm [color="Red (633nm)" package="5 mm [THT]"]
  R13 = Resistor [tolerance=±5% resistance=4.7k package=THT]
  J6 = Camdenboss CTB0158-2 [part_number=CTB0158-2 package=THT]
  Q4 = Basic FET N-Channel [part_number=IRF520N package="TO220 [THT]"]
  LED4 = LED - 5mm [color="Red (633nm)" package="5 mm [THT]"]
  R7 = Resistor [tolerance=±5% resistance=1k package=THT]
  R8 = Resistor [tolerance=±5% resistance=1k package=THT]
  LED3 = LED - 5mm [color="Red (633nm)" package="5 mm [THT]"]
  Q3 = Basic FET N-Channel [part_number=IRF520N package="TO220 [THT]"]
  R5 = Resistor [tolerance=±5% resistance=1k package=THT]
  R6 = Resistor [tolerance=±5% resistance=1k package=THT]
  J10 = Camdenboss CTB0158-2 [part_number=CTB0158-2 package=THT]
  J9 = Camdenboss CTB0158-2 [part_number=CTB0158-2 package=THT]
  J12 = Camdenboss CTB0158-2 [part_number=CTB0158-2 package=THT]
  J13 = Camdenboss CTB0158-2 [part_number=CTB0158-2 package=THT]
  J14 = Camdenboss CTB0158-2 [part_number=CTB0158-2 package=THT]
  J11 = Camdenboss CTB0158-2 [part_number=CTB0158-2 package=THT]
  DHT1 = DHT22 Humidity and Temperature Sensor
  J1 = Camdenboss CTB0158-2 [part_number=CTB0158-2 package=THT]
  J2 = Camdenboss CTB0158-2 [part_number=CTB0158-2 package=THT]
  J4 = Camdenboss CTB0158-2 [part_number=CTB0158-2 package=THT]
  Q2 = Basic FET N-Channel [part_number=IRF520N package="TO220 [THT]"]
  R3 = Resistor [tolerance=±5% resistance=1k package=THT]
  R4 = Resistor [tolerance=±5% resistance=1k package=THT]
  LED2 = LED - 5mm [color="Red (633nm)" package="5 mm [THT]"]
  J3 = Camdenboss CTB0158-2 [part_number=CTB0158-2 package=THT]
  Q1 = Basic FET N-Channel [part_number=IRF520N package="TO220 [THT]"]
  R1 = Resistor [tolerance=±5% resistance=1k package=THT]
  R2 = Resistor [tolerance=±5% resistance=1k package=THT]
  LED1 = LED - 5mm [color="Red (633nm)" package="5 mm [THT]"]
  J15 = female pin header, 3 pins [form="♀ (female)"]
  J5 = Camdenboss CTB0158-2 [part_number=CTB0158-2 package=THT]
  J8 = Camdenboss CTB0158-2 [part_number=CTB0158-2 package=THT]
  J17 = Camdenboss CTB0158-2 [part_number=CTB0158-2 package=THT]
  J15_2 = Camdenboss CTB0158-2 [part_number=CTB0158-2 package=THT]
  J7 = Camdenboss CTB0158-2 [part_number=CTB0158-2 package=THT]

nets:
  3.3V: U1.3.3, R13.Pin_0, J9.pin2, J12.pin2, J14.pin1, J11.pin1, DHT1.VDD, J15.pin1
  N1: U1.GPIO32, J13.pin2
  N2: U1.GPIO33, J12.pin1
  N3: U1.GPIO25, J10.pin2
  N4: U1.GPIO26, J9.pin1
  N5: U1.GPIO14, R13.Pin_1, DHT1.DATA, J15.pin2
  GND: U1.GND, Q5.source, R10.Pin_1, R9.Pin_1, Q6.source, R11.Pin_1, R12.Pin_1, Q4.source, R7.Pin_1, R8.Pin_1, Q3.source, R5.Pin_1, R6.Pin_1, J10.pin1, J13.pin1, J14.pin2, J11.pin2, DHT1.GND, J1.pin1, J2.pin2, Q2.source, R3.Pin_1, R4.Pin_1, Q1.source, R1.Pin_1, R2.Pin_1, J15.pin3, J17.pin2, J15_2.pin2
  5V: U1.VIN, J1.pin2
  N6: U1.GPIO15, J15_2.pin1
  N7: U1.GPIO2, J17.pin1
  N8: U1.GPIO0, Q1.gate, R2.Pin_0, LED1.anode
  N9: U1.GPIO4, U1.GPIO17, Q2.gate, R4.Pin_0, LED2.anode
  N10: U1.GPIO5, LED3.anode, Q3.gate, R6.Pin_0
  N11: U1.GPIO18, Q4.gate, LED4.anode, R8.Pin_0
  N12: U1.GPIO19, Q5.gate, R10.Pin_0, LED5.anode
  N13: U1.GPIO21, Q6.gate, R12.Pin_0, LED6.anode
  N14: Q5.drain, J7.pin1
  N15: LED5.cathode, R9.Pin_0
  N16: Q6.drain, J8.pin1
  N17: R11.Pin_0, LED6.cathode
  N18: J6.pin1, Q4.drain
  12V: J6.pin2, J2.pin1, J4.pin2, J3.pin2, J5.pin2, J8.pin2, J7.pin2
  N19: LED4.cathode, R7.Pin_0
  N20: LED3.cathode, R5.Pin_0
  N21: Q3.drain, J5.pin1
  N22: J4.pin1, Q2.drain
  N23: R3.Pin_0, LED2.cathode
  N24: J3.pin1, Q1.drain
  N25: R1.Pin_0, LED1.cathode

notes:
  G. Benito
  Riego 1.0
  - 12 V +
  + 5V -
  -

custom parts:
  ESP32-38PinWide: Generic 38-Pin ESP32 with wide format (only access to one side of pins on a breadboard) based on Stephen Lilley's HiLetgo ESP-WROOM-32 ESP32 ESP-32S Development Board.
